# Fritzing sketch bicikli (saved by Fritzing 0.9.9b)
breadboards: 1

parts:
  Mod1 = Raspberry Pi 4B
  R1 = Resistor [tolerance=±5% power=0.25 resistance=10k package=THT]
  R2 = Resistor [tolerance=±5% power=0.25 resistance=3.3k package=THT]
  S1 = Pushbutton [package="[THT]"]
  LED1 = RGB LED (com. anode, rbg) [package="5 mm [THT]"]
  R3 = Resistor [tolerance=±5% power=0.25 resistance=3.3k package=THT]

nets:
  N1: Mod1.3V3, R1.Pin_1, LED1.common_anode
  N2: Mod1.GPIO25, R2.Pin_0
  N3: Mod1.GPIO13, R3.Pin_1
  N4: R1.Pin_0, R2.Pin_1, S1.Pin_3, S1.Pin_4
  GND: S1.Pin_2
  N5: LED1.green_cathode, R3.Pin_0
